// Logisim project MIPS_Mono_v5_5-BNE.circ as structural Verilog
module main (
  input  reset
);

  wire clock_out, cpu_1_memrd, cpu_1_memwr;
  wire [15:0] cpu_1_data_address, cpu_1_instruction_address;
  wire [31:0] cpu_1_dataout, ram_1_data, ram_2_data;

  Clock clock (.out(clock_out));
  CPU cpu_1 (
    .reset(reset), .INSTRUCTION(ram_1_data), .memRd(cpu_1_memrd),
    .INSTRUCTION_ADDRESS(cpu_1_instruction_address), .DATAIN(ram_2_data), .DATAOUT(cpu_1_dataout),
    .DATA_ADDRESS(cpu_1_data_address), .clock(clock_out), .memWr(cpu_1_memwr));
  RAM #(.addrWidth(16), .dataWidth(32)) ram_1 (
    .addr(cpu_1_instruction_address), .data(ram_1_data), .clk(clock_out));  // open: sel, ld, clr
  info info_1 ();
  RAM #(.addrWidth(16), .dataWidth(32), .bus("separate")) ram_2 (
    .addr(cpu_1_data_address), .din(cpu_1_dataout), .data(ram_2_data), .str(cpu_1_memwr), .clk(clock_out),
    .ld(cpu_1_memrd));  // open: sel, clr

  // Notes on the sheet:
  //   Text Memory
  //   Data Memory
endmodule

module control (
  input  [5:0] opcode,
  input  [5:0] \function ,
  output [2:0] ALUOP,
  output Branch,
  output MemRD,
  output MemWR,
  output RegWR,
  output [1:0] RegDst,
  output ALUSrc,
  output [2:0] Mem2Reg,
  output mul,
  output div,
  output [1:0] Jump
);

  wire instruction_decode_1_add, instruction_decode_1_addi, instruction_decode_1_and,
       instruction_decode_1_andi, instruction_decode_1_j, instruction_decode_1_jal, instruction_decode_1_jr,
       instruction_decode_1_lui, instruction_decode_1_mfhi, instruction_decode_1_mflo,
       instruction_decode_1_nor, instruction_decode_1_or, instruction_decode_1_ori, instruction_decode_1_sll,
       instruction_decode_1_slt, instruction_decode_1_srl, instruction_decode_1_sub,
       instruction_decode_1_tipo_r, instruction_decode_1_xor, instruction_decode_1_xori, nor_1_out,
       nor_2_out, nor_4_out, or_1_out, or_2_out, or_4_out;
  wire [2:0] controlled_buffer_1_out;

  Instruction_Decode instruction_decode_1 (
    .Tipo_R(instruction_decode_1_tipo_r), .add(instruction_decode_1_add), .addi(instruction_decode_1_addi),
    .sub(instruction_decode_1_sub), .andi(instruction_decode_1_andi), .mult(mul),
    .ori(instruction_decode_1_ori), .div(div), .xori(instruction_decode_1_xori),
    .sll(instruction_decode_1_sll), .beq(Branch), .srl(instruction_decode_1_srl), .j(instruction_decode_1_j),
    .mfhi(instruction_decode_1_mfhi), .lw(MemRD), .mflo(instruction_decode_1_mflo), .sw(MemWR),
    .\and (instruction_decode_1_and), .\or (instruction_decode_1_or), .\nor (instruction_decode_1_nor),
    .\xor (instruction_decode_1_xor), .slt(instruction_decode_1_slt), .jr(instruction_decode_1_jr),
    .opcode(opcode), .\function (\function ), .jal(instruction_decode_1_jal), .lui(instruction_decode_1_lui));
  nor nor_1 (nor_1_out, instruction_decode_1_slt, MemRD, instruction_decode_1_jal, instruction_decode_1_lui, instruction_decode_1_mflo, instruction_decode_1_mfhi);
  nor nor_2 (nor_2_out, or_1_out, instruction_decode_1_jr);
  or or_1 (or_1_out, instruction_decode_1_j, instruction_decode_1_jal);
  assign controlled_buffer_1_out = instruction_decode_1_add ? 3'b000 : 3'bz;  // Controlled_Buffer controlled_buffer_1
  assign controlled_buffer_1_out = instruction_decode_1_sub ? 3'b001 : 3'bz;  // Controlled_Buffer controlled_buffer_2
  assign controlled_buffer_1_out = instruction_decode_1_sll ? 3'b010 : 3'bz;  // Controlled_Buffer controlled_buffer_3
  assign controlled_buffer_1_out = instruction_decode_1_srl ? 3'b011 : 3'bz;  // Controlled_Buffer controlled_buffer_4
  assign controlled_buffer_1_out = instruction_decode_1_and ? 3'b100 : 3'bz;  // Controlled_Buffer controlled_buffer_5
  assign controlled_buffer_1_out = instruction_decode_1_or ? 3'b101 : 3'bz;  // Controlled_Buffer controlled_buffer_6
  assign controlled_buffer_1_out = instruction_decode_1_nor ? 3'b110 : 3'bz;  // Controlled_Buffer controlled_buffer_7
  assign controlled_buffer_1_out = instruction_decode_1_xor ? 3'b111 : 3'bz;  // Controlled_Buffer controlled_buffer_8
  assign controlled_buffer_1_out = instruction_decode_1_addi ? 3'b000 : 3'bz;  // Controlled_Buffer controlled_buffer_9
  assign controlled_buffer_1_out = instruction_decode_1_andi ? 3'b100 : 3'bz;  // Controlled_Buffer controlled_buffer_10
  assign controlled_buffer_1_out = instruction_decode_1_ori ? 3'b101 : 3'bz;  // Controlled_Buffer controlled_buffer_11
  assign controlled_buffer_1_out = instruction_decode_1_xori ? 3'b111 : 3'bz;  // Controlled_Buffer controlled_buffer_12
  assign controlled_buffer_1_out = MemRD ? 3'b000 : 3'bz;  // Controlled_Buffer controlled_buffer_13
  assign controlled_buffer_1_out = MemWR ? 3'b000 : 3'bz;  // Controlled_Buffer controlled_buffer_14
  nor nor_3 (RegWR, Branch, instruction_decode_1_j, MemWR, div, mul, instruction_decode_1_jr);
  nor nor_4 (nor_4_out, or_2_out, instruction_decode_1_lui, instruction_decode_1_jal);
  or or_2 (or_2_out, instruction_decode_1_addi, instruction_decode_1_andi, instruction_decode_1_ori, instruction_decode_1_xori, MemRD, MemWR);
  or or_3 (ALUSrc, instruction_decode_1_addi, instruction_decode_1_andi, instruction_decode_1_ori, instruction_decode_1_xori, MemRD, MemWR);
  assign Mem2Reg = nor_1_out ? 3'b000 : 3'bz;  // Controlled_Buffer controlled_buffer_15
  assign Mem2Reg = instruction_decode_1_slt ? 3'b001 : 3'bz;  // Controlled_Buffer controlled_buffer_16
  assign Mem2Reg = MemRD ? 3'b010 : 3'bz;  // Controlled_Buffer controlled_buffer_17
  assign Mem2Reg = instruction_decode_1_mflo ? 3'b011 : 3'bz;  // Controlled_Buffer controlled_buffer_18
  assign Mem2Reg = instruction_decode_1_mfhi ? 3'b100 : 3'bz;  // Controlled_Buffer controlled_buffer_19
  assign Mem2Reg = instruction_decode_1_jal ? 3'b101 : 3'bz;  // Controlled_Buffer controlled_buffer_20
  assign Mem2Reg = instruction_decode_1_lui ? 3'b110 : 3'bz;  // Controlled_Buffer controlled_buffer_21
  assign Jump = nor_2_out ? 2'b00 : 2'bz;  // Controlled_Buffer controlled_buffer_22
  assign Jump = or_1_out ? 2'b01 : 2'bz;  // Controlled_Buffer controlled_buffer_23
  assign Jump = instruction_decode_1_jr ? 2'b10 : 2'bz;  // Controlled_Buffer controlled_buffer_24
  or or_4 (or_4_out, instruction_decode_1_tipo_r, instruction_decode_1_addi, instruction_decode_1_andi, instruction_decode_1_ori, instruction_decode_1_xori, MemWR, MemRD);
  assign ALUOP = or_4_out ? controlled_buffer_1_out : 3'bz;  // Controlled_Buffer controlled_buffer_25
  instruction_formats instruction_formats_1 ();
  assign RegDst = nor_4_out ? 2'b00 : 2'bz;  // Controlled_Buffer controlled_buffer_26
  assign RegDst = or_2_out ? 2'b01 : 2'bz;  // Controlled_Buffer controlled_buffer_27
  assign RegDst = instruction_decode_1_jal ? 2'b10 : 2'bz;  // Controlled_Buffer controlled_buffer_28
  assign RegDst = instruction_decode_1_lui ? 2'b01 : 2'bz;  // Controlled_Buffer controlled_buffer_29

  // Notes on the sheet:
  //   add
  //   sub
  //   addi
  //   lw
  //   sw
  //   sll
  //   srl
  //   and
  //   or
  //   nor
  //   xor
  //   andi
  //   ori
  //   xori
endmodule

module ALU (
  input  [31:0] A,
  input  [31:0] B,
  input  [2:0] ALUop,
  input  [4:0] shamt,
  output [4:0] FLAGS,
  output [31:0] C
);

  wire [31:0] adder_1_out, and_1_out, nor_1_out, or_1_out, shifter_1_out, shifter_2_out, subtractor_1_out,
       xor_1_out;

  Adder #(.width(32)) adder_1 (.a(A), .b(B), .out(adder_1_out), .cout(FLAGS[1]));  // open: cin
  Subtractor #(.width(32)) subtractor_1 (.a(A), .b(B), .out(subtractor_1_out), .bout(FLAGS[0]));  // open: bin
  Shifter #(.width(32)) shifter_1 (.in(A), .\dist (shamt), .out(shifter_1_out));
  Shifter #(.width(32), .shift("lr")) shifter_2 (.in(A), .\dist (shamt), .out(shifter_2_out));
  assign and_1_out = A & B;  // AND_Gate and_1, 32 bits wide
  assign or_1_out = A | B;  // OR_Gate or_1, 32 bits wide
  assign nor_1_out = ~(A | B);  // NOR_Gate nor_1, 32 bits wide
  assign xor_1_out = A ^ B;  // XOR_Gate xor_1, 32 bits wide
  Comparator #(.width(32)) comparator_1 (.a(A), .b(B), .gt(FLAGS[4]), .eq(FLAGS[3]), .lt(FLAGS[2]));
  Multiplexer #(.select(3), .width(32)) multiplexer_1 (
    .in0(adder_1_out), .in1(subtractor_1_out), .in2(shifter_1_out), .in3(shifter_2_out), .in4(and_1_out),
    .in5(or_1_out), .in6(nor_1_out), .in7(xor_1_out), .out(C), .sel(ALUop));  // open: en

  // Notes on the sheet:
  //   ___________________
  //   |_>_|_=_|_<_|_IO_|_IU_|
endmodule

module RegisterFile (
  input  [4:0] regRead1,
  input  [4:0] regRead2,
  input  [4:0] regWrite,
  input  cRegWrite,
  input  [31:0] writeData,
  input  clk,
  output [31:0] readData1,
  output [31:0] readData2
);

  wire and_1_out, demultiplexer_1_out0, demultiplexer_1_out1, demultiplexer_1_out2, demultiplexer_1_out3;
  wire [31:0] regfile8reg_1_readdata1, regfile8reg_1_readdata2, regfile8reg_2_readdata1,
       regfile8reg_2_readdata2, regfile8reg_3_readdata1, regfile8reg_3_readdata2, zeroreg_1_readdata1,
       zeroreg_1_readdata2;

  and and_1 (and_1_out, 1'b1, cRegWrite);
  Demultiplexer #(.select(2)) demultiplexer_1 (
    .out0(demultiplexer_1_out0), .out1(demultiplexer_1_out1), .out2(demultiplexer_1_out2),
    .out3(demultiplexer_1_out3), .in(and_1_out), .sel(regWrite[4:3]));  // open: en
  zeroReg zeroreg_1 (
    .writeData(writeData), .clk(clk), .cRegWrite(demultiplexer_1_out0), .regWrite(regWrite[2:0]),
    .readData1(zeroreg_1_readdata1), .regRead1(regRead1[2:0]), .readData2(zeroreg_1_readdata2),
    .regRead2(regRead2[2:0]));
  RegFile8reg regfile8reg_1 (
    .writeData(writeData), .clk(clk), .cRegWrite(demultiplexer_1_out1), .regWrite(regWrite[2:0]),
    .readData1(regfile8reg_1_readdata1), .regRead1(regRead1[2:0]), .readData2(regfile8reg_1_readdata2),
    .regRead2(regRead2[2:0]));
  RegFile8reg regfile8reg_2 (
    .writeData(writeData), .clk(clk), .cRegWrite(demultiplexer_1_out2), .regWrite(regWrite[2:0]),
    .readData1(regfile8reg_2_readdata1), .regRead1(regRead1[2:0]), .readData2(regfile8reg_2_readdata2),
    .regRead2(regRead2[2:0]));
  RegFile8reg regfile8reg_3 (
    .writeData(writeData), .clk(clk), .cRegWrite(demultiplexer_1_out3), .regWrite(regWrite[2:0]),
    .readData1(regfile8reg_3_readdata1), .regRead1(regRead1[2:0]), .readData2(regfile8reg_3_readdata2),
    .regRead2(regRead2[2:0]));
  Multiplexer #(.select(2), .width(32)) multiplexer_1 (
    .in0(zeroreg_1_readdata1), .in1(regfile8reg_1_readdata1), .in2(regfile8reg_2_readdata1),
    .in3(regfile8reg_3_readdata1), .out(readData1), .sel(regRead1[4:3]));  // open: en
  Multiplexer #(.select(2), .width(32)) multiplexer_2 (
    .in0(zeroreg_1_readdata2), .in1(regfile8reg_1_readdata2), .in2(regfile8reg_2_readdata2),
    .in3(regfile8reg_3_readdata2), .out(readData2), .sel(regRead2[4:3]));  // open: en
endmodule

module RegFile8reg (
  input  [31:0] writeData,
  input  clk,
  input  cRegWrite,
  input  [2:0] regRead1,
  input  [2:0] regWrite,
  input  [2:0] regRead2,
  output [31:0] readData1,
  output [31:0] readData2
);

  wire and_1_out, demultiplexer_1_out0, demultiplexer_1_out1, demultiplexer_1_out2, demultiplexer_1_out3,
       demultiplexer_1_out4, demultiplexer_1_out5, demultiplexer_1_out6, demultiplexer_1_out7;
  wire [31:0] register_1_q, register_2_q, register_3_q, register_4_q, register_5_q, register_6_q,
       register_7_q, register_8_q;

  Demultiplexer #(.select(3)) demultiplexer_1 (
    .out0(demultiplexer_1_out0), .out1(demultiplexer_1_out1), .out2(demultiplexer_1_out2),
    .out3(demultiplexer_1_out3), .out4(demultiplexer_1_out4), .out5(demultiplexer_1_out5),
    .out6(demultiplexer_1_out6), .out7(demultiplexer_1_out7), .in(and_1_out), .sel(regWrite));  // open: en
  and and_1 (and_1_out, 1'b1, cRegWrite);
  Register #(.width(32)) register_1 (
    .D(writeData), .en(demultiplexer_1_out0), .Q(register_1_q), .clk(clk));  // open: clr
  Register #(.width(32)) register_2 (
    .D(writeData), .en(demultiplexer_1_out1), .Q(register_2_q), .clk(clk));  // open: clr
  Register #(.width(32)) register_3 (
    .D(writeData), .en(demultiplexer_1_out2), .Q(register_3_q), .clk(clk));  // open: clr
  Register #(.width(32)) register_4 (
    .D(writeData), .en(demultiplexer_1_out3), .Q(register_4_q), .clk(clk));  // open: clr
  Register #(.width(32)) register_5 (
    .D(writeData), .en(demultiplexer_1_out4), .Q(register_5_q), .clk(clk));  // open: clr
  Register #(.width(32)) register_6 (
    .D(writeData), .en(demultiplexer_1_out5), .Q(register_6_q), .clk(clk));  // open: clr
  Register #(.width(32)) register_7 (
    .D(writeData), .en(demultiplexer_1_out6), .Q(register_7_q), .clk(clk));  // open: clr
  Register #(.width(32)) register_8 (
    .D(writeData), .en(demultiplexer_1_out7), .Q(register_8_q), .clk(clk));  // open: clr
  Multiplexer #(.select(3), .width(32)) multiplexer_1 (
    .in0(register_1_q), .in1(register_2_q), .in2(register_3_q), .in3(register_4_q), .in4(register_5_q),
    .in5(register_6_q), .in6(register_7_q), .in7(register_8_q), .out(readData1), .sel(regRead1));  // open: en
  Multiplexer #(.select(3), .width(32)) multiplexer_2 (
    .in0(register_1_q), .in1(register_2_q), .in2(register_3_q), .in3(register_4_q), .in4(register_5_q),
    .in5(register_6_q), .in6(register_7_q), .in7(register_8_q), .out(readData2), .sel(regRead2));  // open: en
endmodule

module zeroReg (
  input  [31:0] writeData,
  input  clk,
  input  cRegWrite,
  input  [2:0] regRead1,
  input  [2:0] regWrite,
  input  [2:0] regRead2,
  output [31:0] readData1,
  output [31:0] readData2
);

  wire and_1_out, demultiplexer_1_out0, demultiplexer_1_out1, demultiplexer_1_out2, demultiplexer_1_out3,
       demultiplexer_1_out4, demultiplexer_1_out5, demultiplexer_1_out6, demultiplexer_1_out7;
  wire [31:0] register_1_q, register_2_q, register_3_q, register_4_q, register_5_q, register_6_q,
       register_7_q, register_8_q;

  and and_1 (and_1_out, 1'b1, cRegWrite);
  Demultiplexer #(.select(3)) demultiplexer_1 (
    .out0(demultiplexer_1_out0), .out1(demultiplexer_1_out1), .out2(demultiplexer_1_out2),
    .out3(demultiplexer_1_out3), .out4(demultiplexer_1_out4), .out5(demultiplexer_1_out5),
    .out6(demultiplexer_1_out6), .out7(demultiplexer_1_out7), .in(and_1_out), .sel(regWrite));  // open: en
  Register #(.width(32)) register_1 (
    .D(writeData), .en(demultiplexer_1_out0), .Q(register_1_q), .clr(1'b1));  // open: clk
  Register #(.width(32)) register_2 (
    .D(writeData), .en(demultiplexer_1_out1), .Q(register_2_q), .clk(clk));  // open: clr
  Register #(.width(32)) register_3 (
    .D(writeData), .en(demultiplexer_1_out2), .Q(register_3_q), .clk(clk));  // open: clr
  Register #(.width(32)) register_4 (
    .D(writeData), .en(demultiplexer_1_out3), .Q(register_4_q), .clk(clk));  // open: clr
  Register #(.width(32)) register_5 (
    .D(writeData), .en(demultiplexer_1_out4), .Q(register_5_q), .clk(clk));  // open: clr
  Register #(.width(32)) register_6 (
    .D(writeData), .en(demultiplexer_1_out5), .Q(register_6_q), .clk(clk));  // open: clr
  Register #(.width(32)) register_7 (
    .D(writeData), .en(demultiplexer_1_out6), .Q(register_7_q), .clk(clk));  // open: clr
  Register #(.width(32)) register_8 (
    .D(writeData), .en(demultiplexer_1_out7), .Q(register_8_q), .clk(clk));  // open: clr
  Multiplexer #(.select(3), .width(32)) multiplexer_1 (
    .in0(register_1_q), .in1(register_2_q), .in2(register_3_q), .in3(register_4_q), .in4(register_5_q),
    .in5(register_6_q), .in6(register_7_q), .in7(register_8_q), .out(readData1), .sel(regRead1));  // open: en
  Multiplexer #(.select(3), .width(32)) multiplexer_2 (
    .in0(register_1_q), .in1(register_2_q), .in2(register_3_q), .in3(register_4_q), .in4(register_5_q),
    .in5(register_6_q), .in6(register_7_q), .in7(register_8_q), .out(readData2), .sel(regRead2));  // open: en
endmodule

module MemBankText (
  input  BoW,
  input  [15:0] address,
  output [31:0] DataOut
);

  wire and_1_out, and_2_out, and_3_out, and_4_out, or_1_out;
  wire [7:0] controlled_buffer_1_out, ram_4_data;
  wire [23:0] ram_1_data;
  wire [31:31] controlled_buffer_2_out;

  and and_1 (and_1_out, ~BoW, ~address[1], ~address[0]);  // AND_Gate
  and and_2 (and_2_out, ~BoW, ~address[1], address[0]);  // AND_Gate
  and and_3 (and_3_out, ~BoW, address[1], ~address[0]);  // AND_Gate
  and and_4 (and_4_out, ~BoW, address[1], address[0]);  // AND_Gate
  RAM #(.addrWidth(14), .bus("separate")) ram_1 (
    .addr(address[15:2]), .data(ram_1_data[7:0]), .ld(1'b1));  // open: din, str, sel, clk, clr
  assign controlled_buffer_1_out = and_1_out ? ram_1_data[7:0] : 8'bz;  // Controlled_Buffer controlled_buffer_1
  or or_1 (or_1_out, and_1_out, and_2_out, and_3_out, and_4_out);
  assign controlled_buffer_2_out[31] = or_1_out ? 1'b0 : 1'bz;  // Controlled_Buffer controlled_buffer_2
  RAM #(.addrWidth(14), .bus("separate")) ram_2 (
    .addr(address[15:2]), .data(ram_1_data[15:8]), .ld(1'b1));  // open: din, str, sel, clk, clr
  assign controlled_buffer_1_out = and_2_out ? ram_1_data[15:8] : 8'bz;  // Controlled_Buffer controlled_buffer_3
  RAM #(.addrWidth(14), .bus("separate")) ram_3 (
    .addr(address[15:2]), .data(ram_1_data[23:16]), .ld(1'b1));  // open: din, str, sel, clk, clr
  assign controlled_buffer_1_out = and_3_out ? ram_1_data[23:16] : 8'bz;  // Controlled_Buffer controlled_buffer_4
  RAM #(.addrWidth(14), .bus("separate")) ram_4 (
    .addr(address[15:2]), .data(ram_4_data), .ld(1'b1));  // open: din, str, sel, clk, clr
  assign controlled_buffer_1_out = and_4_out ? ram_4_data : 8'bz;  // Controlled_Buffer controlled_buffer_5
  assign DataOut = or_1_out ? {{24{controlled_buffer_2_out[31]}}, controlled_buffer_1_out} : 32'bz;  // Controlled_Buffer controlled_buffer_6
  assign DataOut = BoW ? {ram_4_data, ram_1_data} : 32'bz;  // Controlled_Buffer controlled_buffer_7

  // Notes on the sheet:
  //   B=0 | W=1
  //   Bank 0
  //   Bank 1
  //   Bank 2
  //   Bank 3
endmodule

module MemBankData (
  input  [31:0] DataIn,
  input  BoW,
  input  [15:0] address,
  input  clock,
  input  R_W,
  output [31:0] DataOut
);

  wire and_1_out, and_2_out, and_3_out, and_4_out, and_5_out, and_6_out, and_7_out, and_8_out, or_1_out,
       or_2_out, or_3_out, or_4_out, or_5_out;
  wire [7:0] controlled_buffer_2_out, multiplexer_1_out, multiplexer_2_out, multiplexer_3_out, ram_1_data,
       ram_2_data;
  wire [31:16] ram_3_data;

  and and_1 (and_1_out, ~BoW, address[1], address[0]);  // AND_Gate
  and and_2 (and_2_out, ~BoW, address[1], ~address[0]);  // AND_Gate
  and and_3 (and_3_out, ~BoW, ~address[1], address[0]);  // AND_Gate
  and and_4 (and_4_out, ~BoW, ~address[1], ~address[0]);  // AND_Gate
  and and_5 (and_5_out, R_W, BoW);
  and and_6 (and_6_out, R_W, BoW);
  and and_7 (and_7_out, R_W, BoW);
  and and_8 (and_8_out, R_W, BoW);
  or or_1 (or_1_out, and_5_out, and_4_out);
  Multiplexer #(.width(8)) multiplexer_1 (
    .in0(DataIn[15:8]), .in1(DataIn[7:0]), .out(multiplexer_1_out), .sel(and_3_out));  // open: en
  or or_2 (or_2_out, and_6_out, and_3_out);
  Multiplexer #(.width(8)) multiplexer_2 (
    .in0(DataIn[23:16]), .in1(DataIn[7:0]), .out(multiplexer_2_out), .sel(and_2_out));  // open: en
  or or_3 (or_3_out, and_7_out, and_2_out);
  Multiplexer #(.width(8)) multiplexer_3 (
    .in0(DataIn[31:24]), .in1(DataIn[7:0]), .out(multiplexer_3_out), .sel(and_1_out));  // open: en
  or or_4 (or_4_out, and_8_out, and_1_out);
  RAM #(.addrWidth(14), .bus("separate")) ram_1 (
    .addr(address[15:2]), .din(DataIn[7:0]), .data(ram_1_data), .str(or_1_out), .clk(clock));  // open: sel, ld, clr
  RAM #(.addrWidth(14), .bus("separate")) ram_2 (
    .addr(address[15:2]), .din(multiplexer_1_out), .data(ram_2_data), .str(or_2_out), .clk(clock));  // open: sel, ld, clr
  RAM #(.addrWidth(14), .bus("separate")) ram_3 (
    .addr(address[15:2]), .din(multiplexer_2_out), .data(ram_3_data[23:16]), .str(or_3_out), .clk(clock));  // open: sel, ld, clr
  RAM #(.addrWidth(14), .bus("separate")) ram_4 (
    .addr(address[15:2]), .din(multiplexer_3_out), .data(ram_3_data[31:24]), .str(or_4_out), .clk(clock));  // open: sel, ld, clr
  assign DataOut = BoW ? {ram_3_data, ram_2_data, ram_1_data} : 32'bz;  // Controlled_Buffer controlled_buffer_1
  assign controlled_buffer_2_out = and_4_out ? ram_1_data : 8'bz;  // Controlled_Buffer controlled_buffer_2
  assign controlled_buffer_2_out = and_3_out ? ram_2_data : 8'bz;  // Controlled_Buffer controlled_buffer_3
  assign controlled_buffer_2_out = and_2_out ? ram_3_data[23:16] : 8'bz;  // Controlled_Buffer controlled_buffer_4
  assign controlled_buffer_2_out = and_1_out ? ram_3_data[31:24] : 8'bz;  // Controlled_Buffer controlled_buffer_5
  assign DataOut = or_5_out ? {{24{1'b0}}, controlled_buffer_2_out} : 32'bz;  // Controlled_Buffer controlled_buffer_6
  or or_5 (or_5_out, and_3_out, and_4_out, and_1_out, and_2_out);

  // Notes on the sheet:
  //   B=0 | W=1
  //   R=0 | W=1
endmodule

module CPU (
  input  reset,
  input  [31:0] INSTRUCTION,
  input  clock,
  input  [31:0] DATAIN,
  output [15:0] INSTRUCTION_ADDRESS,
  output memRd,
  output memWr,
  output [15:0] DATA_ADDRESS,
  output [31:0] DATAOUT
);

  wire and_1_out, and_2_out, control_1_alusrc, control_1_branch, control_1_div, control_1_mul,
       control_1_regwr, or_1_out, or_2_out, undriven;
  wire [1:0] control_1_jump, control_1_regdst;
  wire [2:0] control_1_aluop, control_1_mem2reg;
  wire [4:0] alu_1_flags, bussplit_1_rd, bussplit_1_rs, bussplit_1_rt, bussplit_1_shamt, multiplexer_1_out;
  wire [5:0] bussplit_1_function, bussplit_1_opcode;
  wire [15:0] adder_1_out, bit_extender_3_out, bit_extender_4_out, branchunit_1_out, bussplit_1_imm_2,
       multiplexer_4_out, multiplexer_5_out;
  wire [25:0] bussplit_1_imm;
  wire [31:0] absoluteaddress_1_out, alu_1_c, bit_extender_1_out, bit_extender_2_out, HI_q,
       leadingzeros_1_out, LO_q, mul_div_unit_1_hi, mul_div_unit_1_lo, multiplexer_2_out, multiplexer_3_out,
       registerfile_1_readdata1, shifter_1_out;

  Register #(.width(16)) PC (.D(multiplexer_5_out), .Q(INSTRUCTION_ADDRESS), .clk(clock), .clr(reset));  // open: en
  info info_1 ();
  Adder #(.width(16)) adder_1 (.a(INSTRUCTION_ADDRESS), .b(16'h1), .out(adder_1_out));  // open: cin, cout
  BusSplit bussplit_1 (
    .INSTRUCTION(INSTRUCTION), .\function (bussplit_1_function), .imm_2(bussplit_1_imm_2),
    .rs(bussplit_1_rs), .rt(bussplit_1_rt), .rd(bussplit_1_rd), .opcode(bussplit_1_opcode),
    .imm(bussplit_1_imm), .shamt(bussplit_1_shamt));
  assign bit_extender_1_out = {{16{bussplit_1_imm_2[15]}}, bussplit_1_imm_2};  // Bit_Extender bit_extender_1
  control control_1 (
    .ALUOP(control_1_aluop), .opcode(bussplit_1_opcode), .\function (bussplit_1_function),
    .Branch(control_1_branch), .MemRD(memRd), .MemWR(memWr), .RegWR(control_1_regwr),
    .RegDst(control_1_regdst), .ALUSrc(control_1_alusrc), .Mem2Reg(control_1_mem2reg), .mul(control_1_mul),
    .div(control_1_div), .Jump(control_1_jump));
  Multiplexer #(.select(2), .width(5)) multiplexer_1 (
    .in0(bussplit_1_rd), .in1(bussplit_1_rt), .in2({5{1'b1}}), .out(multiplexer_1_out), .sel(control_1_regdst));  // open: in3, en
  assign bit_extender_2_out = {{16{adder_1_out[15]}}, adder_1_out};  // Bit_Extender bit_extender_2
  RegisterFile registerfile_1 (
    .regRead1(bussplit_1_rs), .regRead2(bussplit_1_rt), .regWrite(multiplexer_1_out),
    .cRegWrite(control_1_regwr), .writeData(multiplexer_3_out), .clk(clock),
    .readData1(registerfile_1_readdata1), .readData2(DATAOUT));
  AbsoluteAddress absoluteaddress_1 (.address(bussplit_1_imm), .PC(bit_extender_2_out), .out(absoluteaddress_1_out));
  BranchUnit branchunit_1 (.PC(INSTRUCTION_ADDRESS), .imm(bussplit_1_imm_2), .out(branchunit_1_out));
  Multiplexer #(.width(32)) multiplexer_2 (
    .in0(DATAOUT), .in1(bit_extender_1_out), .out(multiplexer_2_out), .sel(control_1_alusrc));  // open: en
  Multiplexer #(.select(3), .width(32)) multiplexer_3 (
    .in0(alu_1_c), .in1(leadingzeros_1_out), .in2(DATAIN), .in3(LO_q), .in4(HI_q), .in5(bit_extender_2_out),
    .in6(shifter_1_out), .in7({32{1'b0}}), .out(multiplexer_3_out), .sel(control_1_mem2reg));  // open: en
  Bit_Extender #(.in_width(32), .\type ("sign")) bit_extender_3 (.in(absoluteaddress_1_out), .out(bit_extender_3_out));
  and and_1 (and_1_out, control_1_branch, alu_1_flags[3]);
  leadingZeros leadingzeros_1 (.\bit (alu_1_flags[2]), .out(leadingzeros_1_out));
  ALU alu_1 (
    .A(registerfile_1_readdata1), .B(multiplexer_2_out), .C(alu_1_c), .ALUop(control_1_aluop),
    .FLAGS(alu_1_flags), .shamt(bussplit_1_shamt));
  MUL_DIV_Unit mul_div_unit_1 (
    .A(registerfile_1_readdata1), .B(DATAOUT), .mult(control_1_mul), .div(control_1_div),
    .LO(mul_div_unit_1_lo), .HI(mul_div_unit_1_hi));
  or or_1 (or_1_out, control_1_mul, control_1_div);
  Multiplexer #(.width(16)) multiplexer_4 (
    .in0(adder_1_out), .in1(branchunit_1_out), .out(multiplexer_4_out), .sel(or_2_out));  // open: en
  Bit_Extender #(.in_width(32), .\type ("sign")) bit_extender_4 (
    .in(registerfile_1_readdata1), .out(bit_extender_4_out));
  Bit_Extender #(.in_width(32)) bit_extender_5 (.in(alu_1_c), .out(DATA_ADDRESS));
  Register #(.width(32)) LO (.D(mul_div_unit_1_lo), .en(or_1_out), .Q(LO_q), .clk(clock));  // open: clr
  Register #(.width(32)) HI (.D(mul_div_unit_1_hi), .en(or_1_out), .Q(HI_q), .clk(clock));  // open: clr
  Multiplexer #(.select(2), .width(16)) multiplexer_5 (
    .in0(multiplexer_4_out), .in1(bit_extender_3_out), .in2(bit_extender_4_out), .out(multiplexer_5_out),
    .sel(control_1_jump));  // open: in3, en
  and and_2 (and_2_out, undriven, ~alu_1_flags[3]);  // AND_Gate
  Shifter #(.width(32)) shifter_1 (.in(bit_extender_1_out), .\dist (5'b10000), .out(shifter_1_out));
  or or_2 (or_2_out, and_1_out, and_2_out);

  // Notes on the sheet:
  //   RegDst
  //   Branch
  //   BNE
  //   regWr
  //   ALUOP
  //   ALUSrc
  //   MemToReg
  //   Jump
endmodule

module Instruction_Decode (
  input  [5:0] \function ,
  input  [5:0] opcode,
  output Tipo_R,
  output add,
  output addi,
  output sub,
  output andi,
  output mult,
  output ori,
  output div,
  output xori,
  output sll,
  output beq,
  output srl,
  output j,
  output mfhi,
  output lw,
  output mflo,
  output sw,
  output \and ,
  output jal,
  output \or ,
  output lui,
  output \nor ,
  output \xor ,
  output slt,
  output jr
);

  wire and_12_out, and_13_out, and_14_out, and_15_out, and_16_out, and_17_out, and_18_out, and_19_out,
       and_20_out, and_21_out, and_22_out, and_23_out, and_24_out, and_25_out;

  and and_1 (Tipo_R, ~opcode[0], ~opcode[1], ~opcode[2], ~opcode[3], ~opcode[4], ~opcode[5]);  // AND_Gate
  and and_2 (addi, ~opcode[5], ~opcode[4], opcode[3], ~opcode[2], ~opcode[1], ~opcode[0]);  // AND_Gate
  and and_3 (andi, ~opcode[5], ~opcode[4], opcode[3], opcode[2], ~opcode[1], ~opcode[0]);  // AND_Gate
  and and_4 (ori, ~opcode[5], ~opcode[4], opcode[3], opcode[2], ~opcode[1], opcode[0]);  // AND_Gate
  and and_5 (xori, ~opcode[5], ~opcode[4], opcode[3], opcode[2], opcode[1], ~opcode[0]);  // AND_Gate
  and and_6 (beq, ~opcode[5], ~opcode[4], ~opcode[3], opcode[2], ~opcode[1], ~opcode[0]);  // AND_Gate
  and and_7 (j, ~opcode[5], ~opcode[4], ~opcode[3], ~opcode[2], opcode[1], ~opcode[0]);  // AND_Gate
  and and_8 (lw, opcode[5], ~opcode[4], ~opcode[3], ~opcode[2], opcode[1], opcode[0]);  // AND_Gate
  and and_9 (sw, opcode[5], ~opcode[4], opcode[3], ~opcode[2], opcode[1], opcode[0]);  // AND_Gate
  and and_10 (jal, ~opcode[5], ~opcode[4], ~opcode[3], ~opcode[2], opcode[1], opcode[0]);  // AND_Gate
  and and_11 (lui, ~opcode[5], ~opcode[4], opcode[3], opcode[2], opcode[1], opcode[0]);  // AND_Gate
  and and_12 (and_12_out, \function [5], ~\function [4], ~\function [3], ~\function [2], ~\function [1], ~\function [0]);  // AND_Gate
  and and_13 (and_13_out, \function [5], ~\function [4], ~\function [3], ~\function [2], \function [1], ~\function [0]);  // AND_Gate
  and and_14 (and_14_out, ~\function [5], \function [4], \function [3], ~\function [2], ~\function [1], ~\function [0]);  // AND_Gate
  and and_15 (and_15_out, ~\function [5], \function [4], \function [3], ~\function [2], \function [1], ~\function [0]);  // AND_Gate
  and and_16 (and_16_out, ~\function [5], ~\function [4], ~\function [3], ~\function [2], ~\function [1], ~\function [0]);  // AND_Gate
  and and_17 (and_17_out, ~\function [5], ~\function [4], ~\function [3], ~\function [2], \function [1], ~\function [0]);  // AND_Gate
  and and_18 (and_18_out, ~\function [5], \function [4], ~\function [3], ~\function [2], ~\function [1], ~\function [0]);  // AND_Gate
  and and_19 (and_19_out, ~\function [5], \function [4], ~\function [3], ~\function [2], \function [1], ~\function [0]);  // AND_Gate
  and and_20 (and_20_out, \function [5], ~\function [4], ~\function [3], \function [2], ~\function [1], ~\function [0]);  // AND_Gate
  and and_21 (and_21_out, \function [5], ~\function [4], ~\function [3], \function [2], ~\function [1], \function [0]);  // AND_Gate
  and and_22 (and_22_out, \function [5], ~\function [4], ~\function [3], \function [2], \function [1], \function [0]);  // AND_Gate
  and and_23 (and_23_out, \function [5], ~\function [4], ~\function [3], \function [2], \function [1], ~\function [0]);  // AND_Gate
  and and_24 (and_24_out, \function [5], ~\function [4], \function [3], ~\function [2], \function [1], ~\function [0]);  // AND_Gate
  and and_25 (and_25_out, ~\function [5], ~\function [4], \function [3], ~\function [2], ~\function [1], ~\function [0]);  // AND_Gate
  and and_26 (add, Tipo_R, and_12_out);
  and and_27 (sub, Tipo_R, and_13_out);
  and and_28 (mult, Tipo_R, and_14_out);
  and and_29 (div, Tipo_R, and_15_out);
  and and_30 (sll, Tipo_R, and_16_out);
  and and_31 (srl, Tipo_R, and_17_out);
  and and_32 (mfhi, Tipo_R, and_18_out);
  and and_33 (mflo, Tipo_R, and_19_out);
  and and_34 (\and , Tipo_R, and_20_out);
  and and_35 (\or , Tipo_R, and_21_out);
  and and_36 (\nor , Tipo_R, and_22_out);
  and and_37 (\xor , Tipo_R, and_23_out);
  and and_38 (slt, Tipo_R, and_24_out);
  and and_39 (jr, Tipo_R, and_25_out);

  // Notes on the sheet:
  //   Tipo R
endmodule

module BusSplit (
  input  [31:0] INSTRUCTION,
  output [25:0] imm,
  output [5:0] \function ,
  output [15:0] imm_2,
  output [4:0] rs,
  output [4:0] rt,
  output [4:0] rd,
  output [4:0] shamt,
  output [5:0] opcode
);


  assign \function  = INSTRUCTION[5:0];
  assign imm = INSTRUCTION[25:0];
  assign imm_2 = INSTRUCTION[15:0];
  assign opcode = INSTRUCTION[31:26];
  assign rd = INSTRUCTION[15:11];
  assign rs = INSTRUCTION[25:21];
  assign rt = INSTRUCTION[20:16];
  assign shamt = INSTRUCTION[10:6];

  // Notes on the sheet:
  //   opcode
  //   rt
  //   20:16
  //   rs
  //   25:21
  //   rd
  //   15:11
  //   shamt
  //   10:6
  //   function
  //   5:0
  //   address / const
  //   15:0
endmodule

module leadingZeros (
  input  \bit ,
  output [31:0] out
);


  assign out = {{31{1'b0}}, \bit };
endmodule

module AbsoluteAddress (
  input  [25:0] address,
  input  [31:0] PC,
  output [31:0] out
);


  assign out = {{6{1'b0}}, address};
endmodule

module BranchUnit (
  input  [15:0] PC,
  input  [15:0] imm,
  output [15:0] out
);

  Adder #(.width(16)) adder_1 (.a(PC), .b(imm), .out(out));  // open: cin, cout
endmodule

module MUL_DIV_Unit (
  input  [31:0] A,
  input  [31:0] B,
  input  mult,
  input  div,
  output [31:0] LO,
  output [31:0] HI
);

  wire and_1_out, xor_1_out;
  wire [31:0] divider_1_out, divider_1_rem, multiplier_1_cout, multiplier_1_out;

  Multiplier #(.width(32)) multiplier_1 (.a(A), .b(B), .out(multiplier_1_out), .cout(multiplier_1_cout));  // open: cin
  Divider #(.width(32)) divider_1 (.a(A), .b(B), .out(divider_1_out), .rem(divider_1_rem));  // open: upper
  and and_1 (and_1_out, ~mult, div);  // AND_Gate
  xor xor_1 (xor_1_out, mult, div);
  Multiplexer #(.width(32)) multiplexer_1 (
    .in0(multiplier_1_out), .in1(divider_1_out), .out(LO), .sel(and_1_out), .en(xor_1_out));
  Multiplexer #(.width(32)) multiplexer_2 (
    .in0(multiplier_1_cout), .in1(divider_1_rem), .out(HI), .sel(and_1_out), .en(xor_1_out));
endmodule
